// Digital circuit CORE.dig as structural Verilog
module CORE (
  input  clk,
  input  RST,
  input  CLR,
  input  in_4,
  input  [11:0] MIPCBI,
  input  [15:0] PCBI,
  input  MIPCBE,
  input  PCBE
);

  wire ALUD_CO, ALUDH_OE, ALUDL_OE, ALUS_OE, and_3_out, and_4_out, and_5_out, ASSERT_f, BR_Q, button_1_out,
       CLK_t, CLKR, comparator_1_eq, comparator_1_gt, comparator_1_lt, comparator_2_eq, comparator_3_eq,
       DC_JUMP, DUMP_p5, EXT_p5, IMMED_OE, IRQ_OE, not_1_out, or_1_out, RAM_OE, RAM_WE, RF_HWE, RF_LWE,
       RF_SFR, RFSRCR_WE, ROM_OE, SFR_OE, SR_WE, WR_WE, XRAM_OE;
  wire [2:0] BR_SRC, BUS_SRC, JUMP_TYPE;
  wire [3:0] ALUSD_FUNC, multiplexer_2_out, RF_SRC;
  wire [5:4] multiplexer_2_out_2;
  wire [6:0] and_2_out;
  wire [7:0] BUS_D, IMMED, RF_Q;
  wire [7:4] RFSRCR_q;
  wire [11:0] ADDRESS, MIPC;
  wire [15:0] ADDR_16, PCER_q;
  wire [47:44] DECODER_2_d;

  Decoder #(.Selector_Bits(3)) decoder_1 (
    .sel(BUS_SRC), .out_0(ALUS_OE), .out_1(ALUDL_OE), .out_2(ALUDH_OE), .out_3(IMMED_OE), .out_4(RAM_OE),
    .out_5(XRAM_OE), .out_6(ROM_OE), .out_7(IRQ_OE));
  DCOUTER #(.generic("Bits := 12;")) dcouter_1 (
    .CLK(CLK_t), .CLR(CLR), .CNT(1'b1), .LE(DC_JUMP), .D(ADDRESS), .Q(MIPC));
  Comparator #(.Bits(8)) comparator_1 (
    .a(RF_Q), .b(IMMED), .gt(comparator_1_gt), .eq(comparator_1_eq), .lt(comparator_1_lt));
  assign BUS_D = IMMED_OE ? IMMED : 8'bz;  // Driver driver_1
  assign BUS_D = SFR_OE ? RF_Q : 8'bz;  // Driver driver_2
  // Probe on BUS_D
  PullDown #(.Bits(8)) pulldown_1 (.out(BUS_D));
  PCE PCER (.CLK(CLK_t), .D(BUS_D), .RS(RF_SRC), .LWE(RF_LWE), .HWE(RF_HWE), .Q(PCER_q));
  Multiplexer #(.Selector_Bits(3)) multiplexer_1 (
    .sel(JUMP_TYPE), .in_0(1'b0), .in_1(1'b1), .in_2(comparator_1_gt), .in_3(comparator_1_eq),
    .in_4(comparator_1_lt), .in_5(BR_Q), .in_6(RST), .in_7(1'b0), .out(DC_JUMP));
  ROM #(.AddrBits(12), .Bits(48)) DECODER_2 (
    .A(MIPC), .sel(1'b1),
    .D({DECODER_2_d, IMMED, ADDRESS, JUMP_TYPE, ALUSD_FUNC, RAM_WE, RFSRCR_WE, BR_SRC, SR_WE, WR_WE, BUS_SRC, RF_SFR, RF_HWE, RF_LWE, RF_SRC}));
  Register #(.Bits(8)) RFSRCR (.D(BUS_D), .C(CLK_t), .en(RFSRCR_WE), .Q({RFSRCR_q, and_2_out[3:0]}));
  and and_1 (and_2_out[5], RFSRCR_q[4], RAM_WE);
  and and_2 (and_2_out[6], RFSRCR_q[4], RAM_OE);
  Comparator #(.Bits(12)) comparator_2 (.a(MIPCBI), .b(MIPC), .eq(comparator_2_eq));  // open: gt, lt
  Comparator #(.Bits(16)) comparator_3 (.a(PCBI), .b(PCER_q), .eq(comparator_3_eq));  // open: gt, lt
  and and_3 (and_3_out, comparator_2_eq, MIPCBE);
  and and_4 (and_4_out, comparator_3_eq, PCBE);
  Multiplexer #(.Bits(7)) multiplexer_2 (
    .sel(RF_SFR), .in_0({1'b0, RF_HWE, RF_LWE, RF_SRC}),
    .in_1({and_2_out[6:5], and_2_out[5], and_2_out[3:0]}),
    .out({SFR_OE, multiplexer_2_out_2, multiplexer_2_out}));
  // Probe on MIPC
  // Probe on RF_SRC
  // Probe on RF_LWE
  // Probe on RF_HWE
  // Probe on RF_SFR
  // Probe on BUS_SRC
  // Probe on WR_WE
  // Probe on SR_WE
  // Probe on BR_SRC
  // Probe on RFSRCR_WE
  // Probe on RAM_WE
  // Probe on ALUSD_FUNC
  // Probe on JUMP_TYPE
  // Probe on ADDRESS
  // Probe on IMMED
  ASSERT ASSERT (.C(CLK_t), .D(BUS_D), .A(ADDR_16[15:8]), .WE(RAM_WE), .F(ASSERT_f));
  Button button_1 (.out(button_1_out));
  reg_file RF (
    .CLK(CLK_t), .RS(multiplexer_2_out), .D(BUS_D), .LLE(multiplexer_2_out_2[4]),
    .HLE(multiplexer_2_out_2[5]), .Q(RF_Q));
  // EXTCTL EXT: pin names not known; wires that end beside it: RAM_WE, ADDR_16[15:8], BUS_D, CLK_t, EXT_p5
  // SwitchDT switchdt_1: pin names not known; wires that end beside it: clk, button_1_out, CLKR
  // Probe on RF_Q
  // Probe on EXT_p5
  or or_1 (or_1_out, ASSERT_f, and_3_out, and_4_out);
  reg__sync_clear #(.generic("Bits := 8;")) WR (.D(BUS_D), .CLK(CLK_t), .CLR(CLR), .nLE(WR_WE), .Q(ADDR_16[7:0]));
  reg__sync_clear #(.generic("Bits := 8;")) SR (.D(BUS_D), .CLK(CLK_t), .CLR(CLR), .nLE(SR_WE), .Q(ADDR_16[15:8]));
  // DUMP DUMP: pin names not known; wires that end beside it: RAM_WE, ADDR_16[15:8], BUS_D, CLK_t, DUMP_p5
  STALL STALL (.C(CLKR), .S(or_1_out), .G(in_4), .O(CLK_t));
  not not_1 (not_1_out, CLK_t);
  // Probe on DUMP_p5
  // Probe on ADDR_16[7:0]
  // Probe on ADDR_16[15:8]
  and and_5 (and_5_out, RAM_WE, CLK_t, not_1_out);
  ALU ALU (
    .A(RF_Q), .B(ADDR_16[7:0]), .S(ALUSD_FUNC), .CI(BR_Q), .nSOE(ALUS_OE), .nDLOE(ALUDL_OE),
    .nDHOE(ALUDH_OE), .O(BUS_D), .CO(ALUD_CO));
  ROM #(.AddrBits(16), .Bits(8)) ROM (.A(ADDR_16), .sel(ROM_OE), .D(BUS_D));
  RAMSinglePortSel #(.AddrBits(7), .isProgramMemory("true"), .Bits(8)) RAM (
    .A(ADDR_16[14:8]), .CS(~ADDR_16[15]), .WE(and_5_out), .OE(RAM_OE), .D(BUS_D));
  BR BR (.CLK(CLK_t), .CLR(CLR), .S(BR_SRC), .ALUDF(ALUD_CO), .ALUSF(ALUD_CO), .A0(RF_Q[0]), .A7(RF_Q[7]), .Q(BR_Q));

  // Other names for the same wires on the sheet: ADDR_RAM[7:0] = ADDR_16[15:8]; GO = in_4

  // Notes on the sheet:
  //   clk: Hz: 2147483647
  //   contents of DECODER_2 (hex, n*v repeats v):
  //   33cc80488,80889,33a,85106,1c30b5,1e54b8,1e08b9,8019980000a,c00a380000a,e003580000a,
  //   f002080000a,f800f80000a,80485,1a088a,324290086,f401d80000a,f601580000a,80485,18088a,
  //   a00,324290086,f501c80000a,b3c,6800c,80486,b30c0,1e50b8,3243e00b9,3243c0136,f201f80000a,
  //   f301f80000a,f031840000a,e802480000a,80485,1a088a,324200236,e403280000a,e602a80000a,
  //   80485,18088a,a00,324200236,e503180000a,b3c,6800c,640,a30b6,1e50b8,3243e00b9,3242001b6,
  //   e203480000a,e303480000a,e031240000a,d007380000a,d804280000a,33c,80485,1a088a,23d,
  //   13003d,132280300d,8348c,450b8,1e20b9,658c,3242600b9,d405b80000a,d604c80000a,80485,
  //   18088a,a00,23c,80486,f008c,8048c,3242e00b6,d505680000a,b3c,6800c,640,a00bd,12043d,
  //   b00c0,132080358d,1e54b8,1943e08b9,405,250b6,5aa03000,324200000,324380035,d206980000a,
  //   d305f80000a,3000,324380035,73c,a00bd,16003d,14083c,6800c,3640,c048d,b30c0,1e50b8,
  //   3243e00b9,d031840000a,33c,80880,600,8088c,6800c,b00c0,123030,1e50b8,3243e00b9,c807980000a,
  //   80485,1a088a,600,90086,3242a00b6,c408d80000a,c608180000a,80485,18088a,a00,80486,236,
  //   3242b0080,c508c80000a,b3c,6800c,640,a00bc,80486,b00c0,8048c,a30b6,1e50b8,3243e00b9,
  //   3243e0036,c209b80000a,c309180000a,2000,324380035,73c,a00bd,16003d,14083c,6800c,2640,
  //   c048d,b30c0,1e50b8,3243e00b9,c031240000a,b3c,6800c,640,100830,b3080,1e50b8,3243e00b9,
  //   a012280000a,b00ef80000a,b80b180000a,33d,80485,1a088a,23c,8248d,654bc,180035,a510c,
  //   1320a03580,1e54b8,1943e08b9,b40d280000a,b60bf80000a,33d,80485,18088a,a00,23c,8248d,
  //   654bc,180035,a510c,1320a03580,1e54b8,1943e08b9,b50ca80000a,b3c,6800c,2640,65486,180035,
  //   a00bc,a510c,1320a03580,1e54b8,1943e08b9,2700,65486,180035,a00bc,a510c,1320a03580,
  //   1e54b8,1943e08b9,b20e280000a,b30d680000a,1c5105,324380035,73c,a00bd,16003d,14083c,
  //   6800c,640,e510d,1000,c048d,b30c0,1e50b8,3243e00b9,b031840000a,73c,a00bd,16003d,14083c,
  //   6800c,640,e013d,1c050d,1a5105,183035,1e50b8,3243e00b9,a80f980000a,b3c,6800c,640,a00bc,
  //   80485,1a088a,9308c,1e50b8,3243e00b9,a410680000a,a610580000a,b3c,6800c,640,a00bc,80485,
  //   18088a,a00,9308c,1e50b8,3243e00b9,a510680000a,a211580000a,a310b80000a,3000,1e50b1,
  //   3243e00b2,73c,a00bd,16003d,14083c,6800c,640,e510d,183035,1e50b8,3243e00b9,a031240000a,
  //   73c,a00bd,16003d,14083c,6800c,640,e013d,1c050d,185105,183035,1e50b8,3243e00b9,9016380000a,
  //   9812d80000a,86485,1a088a,63d,60506,a00bc,40c,1200b5,8048d,3242600b6,9414d80000a,9613980000a,
  //   86485,18088a,a00,63d,60506,a00bc,40c,1200b5,8048d,3242600b6,9514580000a,6005,b3c,
  //   6800c,640,a00bd,60506,a00bc,40c,1200b5,8048d,3222630b6,6005,73d,60506,a00bc,40c,1200b5,
  //   8048d,3222630b6,9215e80000a,9315380000a,82486,45481,1e0882,324200336,6005,73c,a00bd,
  //   16003d,14083c,6800c,640,c048d,b30c0,1e50b8,3243e00b9,9031840000a,3332,1e54b8,1e08b9,
  //   322203331,8816b80000a,33c,80485,1a088a,600,6800c,8088c,3222b30c0,8418280000a,8617780000a,
  //   33c,80485,18088a,a00,600,6800c,8088c,b30c0,1e50b8,3243e00b9,8518280000a,b3c,6800c,
  //   640,a30bd,1e54b8,1e08b9,b3c,8048d,6800c,3222b30c0,8219380000a,8318880000a,82486,45488,
  //   1e0889,324200336,73c,a00bd,16003d,14083c,6800c,640,e050d,1a5105,183035,1e50b8,3243e00b9,
  //   8031240000a,373c,450b8,1e20b9,658c,3242600b9,4024780000a,601f380000a,701cb80000a,
  //   781a180000a,33c,80485,1a088a,32229308c,741b180000a,761a880000a,33c,80485,18088a,a00,
  //   32229308c,751b080000a,333c,1e54b8,1e08b9,700,6800c,8088c,3222b30c0,322203336,721c380000a,
  //   731b880000a,82486,45481,a00b8,1e0482,3242a00b9,73c,a00bd,16003d,14083c,6800c,640,
  //   e050d,185105,183035,1e50b8,3243e00b9,7031840000a,a5006,322a03000,373c,450b8,1e20b9,
  //   658c,3242600b9,681d080000a,80485,1a088a,600,3242000b6,641de80000a,661d780000a,80485,
  //   18088a,a00,600,3242000b6,651dc80000a,b3c,6800c,640,3222030b6,700,3222030b6,621ee80000a,
  //   631e980000a,333c,1e54b8,1e08b9,33d,8088c,6800c,640,48d,3222b30c0,b3c,6800c,640,486,
  //   3222b30c0,6031240000a,a5006,194a03000,1e50b8,3243e00b9,5021f80000a,581f980000a,80485,
  //   1a088a,600,3243a0136,5420780000a,5620080000a,80485,18088a,a00,600,3243a0136,5520580000a,
  //   b3c,6800c,640,3223a3136,700,3223a3136,5221780000a,5321280000a,333c,1e54b8,1e08b9,
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  //   contents of ROM (hex, n*v repeats v):
  //   75,81,0,75,82,0,75,83,0,75,d0,0,75,e0,0,75,f0,0,75,0,1e,75,1,73,75,2,f1,75,3,e8,75,
  //   4,9e,75,5,2b,75,6,e5,75,7,3b,75,8,2b,75,9,18,75,a,fc,75,b,d9,75,c,6f,75,d,39,75,e,
  //   ce,75,f,7a,75,10,d1,75,11,c2,75,12,cf,75,13,27,75,14,2,75,15,be,75,16,8c,75,17,0,
  //   75,18,62,75,19,9d,75,1a,30,75,1b,80,75,1c,43,75,1d,77,75,1e,b,75,1f,40,75,20,8,75,
  //   21,d1,75,22,ff,75,23,c7,75,24,bb,75,25,b5,75,26,c6,75,27,45,75,28,9e,75,29,dc,75,
  //   2a,d3,75,2b,cb,75,2c,51,75,2d,76,75,2e,31,75,2f,d8,75,30,b3,75,31,2f,75,32,31,75,
  //   33,22,75,34,1b,75,35,2e,75,36,fb,75,37,da,75,38,55,75,39,60,75,3a,b6,75,3b,92,75,
  //   3c,c5,75,3d,65,75,3e,5b,75,3f,93,75,40,ee,75,41,f0,75,42,dc,75,43,75,75,44,15,75,
  //   45,4c,75,46,69,75,47,b9,75,48,ba,75,49,3f,75,4a,de,75,4b,82,75,4c,86,75,4d,85,75,
  //   4e,24,75,4f,5e,75,50,a9,75,51,c2,75,52,b1,75,53,21,75,54,df,75,55,f1,75,56,c8,75,
  //   57,83,75,58,e8,75,59,d8,75,5a,d9,75,5b,c7,75,5c,2f,75,5d,96,75,5e,de,75,5f,16,75,
  //   60,5c,75,61,52,75,62,5e,75,63,d7,75,64,e7,75,65,b9,75,66,ee,75,67,74,75,68,48,75,
  //   69,f9,75,6a,df,75,6b,1a,75,6c,e0,75,6d,10,75,6e,33,75,6f,d4,75,70,b6,75,71,2a,75,
  //   72,21,75,73,6,75,74,2c,75,75,66,75,76,d6,75,77,da,75,78,f7,75,79,87,75,7a,4f,75,7b,
  //   7b,75,7c,9c,75,7d,e0,75,7e,2d,75,7f,b7,75,81,2,75,82,22,75,83,c3,75,a8,98,75,b8,92,
  //   75,d0,d4,75,e0,62,75,f0,bd,80,6,d5,1f,15,75,ff,4,d5,13,9,75,ff,4,d5,56,15,75,ff,4,
  //   d5,3f,9,75,ff,4,d5,c,f1,75,ff,4,d5,54,df,75,ff,4,d5,8,3,75,ff,4,75,0,c8,75,1,c6,75,
  //   2,69,75,3,82,75,4,6b,75,5,bc,75,6,38,75,7,80,75,8,cd,75,9,d8,75,a,82,75,b,a9,75,c,
  //   7,75,d,f3,75,e,e0,75,f,d2,75,10,d1,75,11,8a,75,12,db,75,13,7,75,14,89,75,15,1,75,
  //   16,95,75,17,c1,75,18,a5,75,19,ef,75,1a,94,75,1b,7b,75,1c,be,75,1d,8,75,1e,32,75,1f,
  //   29,75,20,2e,75,21,50,75,22,e8,75,23,a7,75,24,4c,75,25,aa,75,26,c5,75,27,2a,75,28,
  //   62,75,29,b4,75,2a,4e,75,2b,69,75,2c,a9,75,2d,21,75,2e,eb,75,2f,bc,75,30,71,75,31,
  //   7f,75,32,72,75,33,19,75,34,be,75,35,f,75,36,79,75,37,9b,75,38,f2,75,39,7c,75,3a,a1,
  //   75,3b,93,75,3c,29,75,3d,16,75,3e,cd,75,3f,2c,75,40,82,75,41,f5,75,42,3f,75,43,d1,
  //   75,44,28,75,45,66,75,46,80,75,47,6,75,48,44,75,49,fe,75,4a,32,75,4b,38,75,4c,b0,75,
  //   4d,e6,75,4e,b9,75,4f,d4,75,50,ca,75,51,ce,75,52,6d,75,53,5b,75,54,7a,75,55,22,75,
  //   56,a4,75,57,2e,75,58,21,75,59,e3,75,5a,f3,75,5b,a4,75,5c,16,75,5d,5b,75,5e,8a,75,
  //   5f,16,75,60,f3,75,61,43,75,62,0,75,63,80,75,64,5c,75,65,fe,75,66,75,75,67,da,75,68,
  //   5a,75,69,20,75,6a,b4,75,6b,d0,75,6c,11,75,6d,10,75,6e,39,75,6f,45,75,70,45,75,71,
  //   c3,75,72,c8,75,73,55,75,74,d9,75,75,87,75,76,8d,75,77,7f,75,78,aa,75,79,c1,75,7a,
  //   ee,75,7b,f,75,7c,2a,75,7d,59,75,7e,94,75,7f,4,75,81,4e,75,82,eb,75,83,aa,75,a8,96,
  //   75,b8,22,75,d0,dd,75,e0,93,75,f0,8b,80,1e,d5,1e,f,75,ff,4,d5,4f,21,75,ff,4,d5,5e,
  //   f1,75,ff,4,d5,1c,f,75,ff,4,d5,48,eb,75,ff,4,d5,1e,eb,75,ff,4,d5,55,f1,75,ff,4,75,
  //   0,81,75,1,6f,75,2,3f,75,3,78,75,4,35,75,5,a2,75,6,d8,75,7,b8,75,8,4a,75,9,9b,75,a,
  //   de,75,b,38,75,c,bd,75,d,98,75,e,cd,75,f,ac,75,10,39,75,11,c8,75,12,75,75,13,67,75,
  //   14,3,75,15,8d,75,16,65,75,17,e6,75,18,eb,75,19,2b,75,1a,f2,75,1b,7e,75,1c,d4,75,1d,
  //   d5,75,1e,9b,75,1f,6e,75,20,a3,75,21,f,75,22,20,75,23,7c,75,24,9b,75,25,5b,75,26,c8,
  //   75,27,70,75,28,eb,75,29,dd,75,2a,6a,75,2b,53,75,2c,e5,75,2d,30,75,2e,6e,75,2f,4,75,
  //   30,b9,75,31,cc,75,32,31,75,33,ff,75,34,66,75,35,76,75,36,aa,75,37,cf,75,38,38,75,
  //   39,28,75,3a,95,75,3b,3f,75,3c,b9,75,3d,a7,75,3e,67,75,3f,33,75,40,f2,75,41,3c,75,
  //   42,81,75,43,80,75,44,28,75,45,e3,75,46,74,75,47,3c,75,48,4f,75,49,3,75,4a,ff,75,4b,
  //   34,75,4c,2b,75,4d,6,75,4e,43,75,4f,ee,75,50,76,75,51,33,75,52,c6,75,53,5b,75,54,fc,
  //   75,55,17,75,56,35,75,57,55,75,58,24,75,59,89,75,5a,bc,75,5b,48,75,5c,57,75,5d,d1,
  //   75,5e,cf,75,5f,26,75,60,5,75,61,8f,75,62,23,75,63,de,75,64,5f,75,65,9,75,66,c3,75,
  //   67,32,75,68,95,75,69,5b,75,6a,4c,75,6b,75,75,6c,f1,75,6d,aa,75,6e,11,75,6f,9d,75,
  //   70,23,75,71,51,75,72,f2,75,73,76,75,74,9,75,75,18,75,76,d8,75,77,f8,75,78,18,75,79,
  //   17,75,7a,fc,75,7b,72,75,7c,c5,75,7d,8c,75,7e,2,75,7f,75,75,81,cd,75,82,dd,75,83,5,
  //   75,a8,fa,75,b8,a1,75,d0,9b,75,e0,f3,75,f0,44,80,c,d5,66,1b,75,ff,4,d5,6,21,75,ff,
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endmodule
